// Logisim project 16CO125-L1.circ as structural Verilog: 1 circuit, main circuit main
module main (
  input  A,
  input  B,
  input  C,
  input  D,
  output A_prime_B_prime_C,
  output X,
  output C_2,
  output Z
);

  wire and_1_out, not_1_out, not_2_out, not_3_out;

  not not_1 (not_1_out, A);
  not not_2 (not_2_out, B);
  and and_1 (and_1_out, not_1_out, not_2_out);
  not not_3 (not_3_out, C);
  xor xor_1 (X, B, C);
  not not_4 (Z, D);
  and and_2 (A_prime_B_prime_C, and_1_out, not_3_out);

  assign C_2 = C;

  // Notes on the sheet:
  //   A`
  //   B`
  //   B
  //   C
  //   A`B`
  //   C`
  //   BC` + B`C
  //   D`
  //   W
  //   Y
endmodule
