// Logisim project 16CO125-L2.circ as structural Verilog: 1 circuit, main circuit main
module main (
  input  A3,
  input  A2,
  input  A1,
  input  A0,
  input  B3,
  input  B2,
  input  B1,
  input  B0,
  output out_9,
  output out_10,
  output out_11
);

  wire and_1_out, and_2_out, and_3_out, and_4_out, not_1_out, not_2_out, not_3_out, not_4_out, xnor_1_out,
       xnor_3_out, xnor_4_out;

  not not_1 (not_1_out, B0);
  not not_2 (not_2_out, B1);
  not not_3 (not_3_out, B2);
  not not_4 (not_4_out, B3);
  xnor xnor_1 (xnor_1_out, B0, A0);
  xnor xnor_2 (not_1_out, B1, A1);
  xnor xnor_3 (xnor_3_out, B2, A2);
  xnor xnor_4 (xnor_4_out, B3, A3);
  and and_1 (and_1_out, not_1_out, not_1_out, xnor_3_out, xnor_4_out, A0);
  and and_2 (and_2_out, not_2_out, xnor_3_out, A1, xnor_4_out);
  buf and_3 (and_3_out, xnor_4_out);  // AND_Gate
  and and_4 (and_4_out, not_4_out, A3);
  and and_5 (out_9, xnor_1_out, not_1_out, xnor_3_out, xnor_4_out);
  or or_1 (out_10, and_1_out, and_2_out, and_3_out, and_4_out);
  nor nor_1 (out_11, out_9, out_10);

  // Notes on the sheet:
  //   B0'
  //   B1'
  //   B2'
  //   B3'
  //   X0
  //   X1
  //   X2
  //   X3
  //   4 BIT MAGNITUDE COMPARATOR
  //   Y0
  //   Y1
  //   Y2
  //   Y3
  //   X0X1X2X3
  //   Y2=X3A2B2'
  //   Y3=A3B3'
  //   Xi=AiBi + Ai'Bi'
  //   Y0=X3X2X1A0B0'
  //   Y1=X3X2A1B1'
  //   Y0+Y1+Y2+Y3
  //   A=B
  //   A>B
  //   A<B
endmodule
