// Logisim project 16CO125-L3.circ as structural Verilog: 1 circuit, main circuit main
module main (
  input  D,
  output Q,
  output Q_prime
);

  wire and_1_out, and_2_out, Clock_out, nor_1_out;

  nor nor_1 (nor_1_out, D, D);
  Clock #(.highDuration(4), .lowDuration(4)) Clock (.out(Clock_out));
  and and_1 (and_1_out, nor_1_out, Clock_out);
  and and_2 (and_2_out, Clock_out, D);
  nor nor_2 (Q, and_1_out, Q_prime);
  nor nor_3 (Q_prime, Q, and_2_out);

  // Notes on the sheet:
  //   D FlipFlop using AND and NOR Gates
endmodule
