// Logisim project 16CO125-L4.circ as structural Verilog: 1 circuit, main circuit main
module main (
  output D3,
  output D2,
  output D1,
  output D0
);

  wire and_1_out, and_2_out, Clock_out, not_1_out, not_2_out, or_1_out, or_2_out, xor_1_out;

  Clock #(.highDuration(4), .lowDuration(4)) Clock (.out(Clock_out));
  and and_1 (and_1_out, not_1_out, not_2_out);
  T_Flip_Flop A (.clk(Clock_out), .T(and_1_out), .Q(D3));  // open: Qn, preset, reset, en
  not not_1 (not_1_out, D1);
  not not_2 (not_2_out, D0);
  or or_1 (or_1_out, D3, D0);
  T_Flip_Flop B (.clk(Clock_out), .T(or_1_out), .Q(D2));  // open: Qn, preset, reset, en
  xor xor_1 (xor_1_out, D0, D1);
  T_Flip_Flop C (.clk(Clock_out), .T(xor_1_out), .Q(D1));  // open: Qn, preset, reset, en
  or or_2 (or_2_out, and_2_out, D3);
  and and_2 (and_2_out, D1, D2);
  T_Flip_Flop D (.clk(Clock_out), .T(or_2_out), .Q(D0));  // open: Qn, preset, reset, en

  // Notes on the sheet:
  //   NOTE: Set the ticks to 4 for better output
  //   COUNTER WITH SEQUENCE 0,8,5,3,7,2
  //   USING T-FlipFlop
  //   EQUATIONS
  //   Ta = (~D1)(~D0)
  //   Tb = (D3 + D0)
  //   Tc = D0(~D1) + D1(~D0)
  //   Td = D3 + D2.D1
endmodule
