// Logisim project 16CO125-L5.circ as structural Verilog: 1 circuit, main circuit main
module main (
  input  I3,
  input  I2,
  input  I1,
  input  I0,
  output O3,
  output O2,
  output O1,
  output O0
);

  wire Clock_out, not_1_out, not_2_out, not_3_out, not_4_out;

  Clock Clock (.out(Clock_out));
  not not_1 (not_1_out, Clock_out);
  D_Flip_Flop d_ff_1 (.clk(not_1_out), .D(I3), .Q(O3));  // open: Qn, preset, en, reset
  not not_2 (not_2_out, Clock_out);
  not not_3 (not_3_out, Clock_out);
  D_Flip_Flop d_ff_2 (.clk(not_2_out), .D(I2), .Q(O2));  // open: Qn, preset, en, reset
  D_Flip_Flop d_ff_3 (.clk(not_3_out), .D(I1), .Q(O1));  // open: Qn, preset, en, reset
  not not_4 (not_4_out, Clock_out);
  D_Flip_Flop d_ff_4 (.clk(not_4_out), .D(I0), .Q(O0));  // open: Qn, preset, en, reset

  // Notes on the sheet:
  //   PIPO Shift Register
  //   Ii = Input i
  //   Oi = Output i
endmodule
