// Logisim project 16CO125-L.circ as structural Verilog: 1 circuit, main circuit main
module main (
  output O2,
  output O1,
  output O0
);

  wire and_1_out, Clock_out, j_k_ff_1_qn, j_k_ff_2_qn;

  Clock Clock (.out(Clock_out));
  J_K_Flip_Flop j_k_ff_1 (
    .J(1'b1), .clk(Clock_out), .K(1'b1), .Q(O0), .Qn(j_k_ff_1_qn), .reset(and_1_out));  // open: preset, en
  and and_1 (and_1_out, O2, O1);
  J_K_Flip_Flop j_k_ff_2 (
    .J(1'b1), .clk(j_k_ff_1_qn), .K(1'b1), .Q(O1), .Qn(j_k_ff_2_qn), .reset(and_1_out));  // open: preset, en
  J_K_Flip_Flop j_k_ff_3 (.J(1'b1), .clk(j_k_ff_2_qn), .K(1'b1), .Q(O2), .reset(and_1_out));  // open: Qn, preset, en

  // Notes on the sheet:
  //   IRREGULAR BINARY COUNT SEQUENCE
  //   MOD 6 COUNTER
  //   Submitted by: 16CO125
endmodule
